# Fritzing sketch schematic (saved by Fritzing 0.9.10b)
perfboards: 1

parts:
  R3 = Resistor [tolerance=±5% power=0.25 resistance=22k package=THT]
  R4 = Trimmer Potentiometer [maximum_resistance=10kΩ knob_status=50% power=0.5W package=THT]
  R5 = Resistor [tolerance=±5% power=0.25 resistance=22k package=THT]
  R6 = Resistor [tolerance=±5% power=0.25 resistance=470k package=THT]
  LM1 = LM741 [part_number=LM741 package="DIP (Dual Inline) [THT]"]
  R7 = Resistor [tolerance=±5% power=0.25 resistance=10 package=THT]
  R8 = Resistor [tolerance=±5% power=0.25 resistance=1k package=THT]
  R9 = Resistor [tolerance=±5% power=0.25 resistance=1k package=THT]
  R10 = Resistor [tolerance=±5% power=0.25 resistance=1k package=THT]
  R11 = Resistor [tolerance=±5% power=0.25 resistance=1k package=THT]
  J4 = male pin header, 2 pins [form="♂ (male)"]
  Probe = top view banana jack black [package=THT]
  Probe_2 = top view banana jack black [package=THT]
  J7 = male pin header, 2 pins [form="♂ (male)"]
  J8 = male pin header, 2 pins [form="♂ (male)"]
  LED3 = smd LED [color="Green (560nm)" package="0603 [SMD]"]
  LED4 = smd LED [color="Red (633nm)" package="0603 [SMD]"]
  J14 = Piezo Speaker
  J9 = male pin header, 2 pins [form="♂ (male)"]
  J15 = male pin header, 2 pins [form="♂ (male)"]
  S6 = Pushbutton [package=THT]
  VCC3 = Battery block 9V
  J16 = male pin header, 2 pins [form="♂ (male)"]

nets (from the schematic view):
  N1: R3.Pin_0, R6.Pin_0, LM1.pin7, J7.pin1, J8.pin1, LED3.anode, J14.pin2
  N2: R3.Pin_1, R7.Pin_0, R9.Pin_1, J4.pin1, Probe.pin1
  N3: R4.leg1, LM1.pin3, R9.Pin_0
  N4: R4.wiper, R6.Pin_1
  N5: R4.leg2, LM1.pin2, R8.Pin_0
  N6: R5.Pin_0, R7.Pin_1, R8.Pin_1, J4.pin2, Probe_2.pin1
  N7: R5.Pin_1, LM1.pin4
  N8: LM1.pin6, R10.Pin_1, J7.pin2, J14.pin1
  N9: R10.Pin_0, J8.pin2, LED3.cathode
  N10: R11.Pin_0, J15.pin2, VCC3.+
  N11: R11.Pin_1, LED4.anode, J9.pin1
  N12: LED4.cathode, J9.pin2, S6.leg1, J16.pin1
  N13: J15.pin1, S6.leg0, VCC3.-, J16.pin2

custom parts:
  LM741: This is a single Op Amp DIP.
  top view banana jack black: Top view banana jack black.
